# Fritzing sketch Barometro (saved by Fritzing 0.9.2b)
breadboards: 1

parts:
  Parte1 = Arduino Uno (Rev3)
  Parte2 = Barometric Pressure Sensor - BMP180 Breakout (GY-68)

nets:
  N1: Parte1.A4/SDA, Parte2.GND
  N2: Parte1.A5/SCL, Parte2.VCC
  N3: Parte1.3V3, Parte2.SCL
  N4: Parte1.GND, Parte2.SDA
